# Fritzing sketch ESP32_I2C_LCD (saved by Fritzing 1.0.3b)

parts:
  M1 = DOIT Esp32 DevKit v1 (30 pins long, 11 pins width) [part_number=ESP32S-PIN30]
  LCM1602_IIC1 = LCM1602 IIC [part_number="LCM1602 IIC" chip_label="LCM1602 IIC" package="DIP (Dual Inline) [THT]"]
  U1 = LCD-16X2 [package=lcd-16x2_noholes]

nets:
  GND: M1.GND, LCM1602_IIC1.GND
  N1: M1.D21, LCM1602_IIC1.SDA
  N2: M1.D22, LCM1602_IIC1.SCL
  VIN: M1.VIN, LCM1602_IIC1.VCC
  VSS: LCM1602_IIC1.VSS, U1.VSS
  VDD: LCM1602_IIC1.VDD, U1.VDD
  N3: LCM1602_IIC1.V0, U1.VO
  N4: LCM1602_IIC1.RS, U1.RS
  N5: LCM1602_IIC1.RW, U1.R_W
  N6: LCM1602_IIC1.E, U1.E
  N7: LCM1602_IIC1.D0, U1.DB0
  N8: LCM1602_IIC1.D1, U1.DB1
  N9: LCM1602_IIC1.D2, U1.DB2
  N10: LCM1602_IIC1.D3, U1.DB3
  N11: LCM1602_IIC1.D4, U1.DB4
  N12: LCM1602_IIC1.D5, U1.DB5
  N13: LCM1602_IIC1.D6, U1.DB6
  N14: LCM1602_IIC1.D7, U1.DB7
  N15: LCM1602_IIC1.A, U1.A
  N16: LCM1602_IIC1.K, U1.K
  N17: LCM1602_IIC1.LED_A, LCM1602_IIC1.LED_B

custom parts:
  DOIT Esp32 DevKit v1 (30 pins long, 11 pins width): The DOIT Esp32 DevKit v1 is one of the development board created by DOIT to evaluate the ESP-WROOM-32 module. It is based on the ESP32 microcontroller that boasts Wifi, Bluetooth, Ethernet and Low Power support all in a single chip. (vanepp) made breadboard work, adjusted pin numbering and labels and reduced size of schematic and cleaned up pcb. This chip is 30pins long (2 x15) and 11 pins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
  LCM1602 IIC: I2C-Module to use a 1602 or 2004 LCD on with the wire.h libory Serial LCD Modul
