# Fritzing sketch ESP32_Keypad (saved by Fritzing 1.0.3b)

parts:
  M1 = DOIT Esp32 DevKit v1 (30 pins long, 11 pins width) [part_number=ESP32S-PIN30]
  Keypad4x2 = Keypad Membran 4x4

nets:
  N1: M1.D32, Keypad4x2.Pin8
  N2: M1.D33, Keypad4x2.Pin7
  N3: M1.D25, Keypad4x2.Pin6
  N4: M1.D26, Keypad4x2.Pin5
  N5: M1.D27, Keypad4x2.Pin4
  N6: M1.D14, Keypad4x2.Pin3
  N7: M1.D12, Keypad4x2.Pin2
  N8: M1.D13, Keypad4x2.Pin1

custom parts:
  DOIT Esp32 DevKit v1 (30 pins long, 11 pins width): The DOIT Esp32 DevKit v1 is one of the development board created by DOIT to evaluate the ESP-WROOM-32 module. It is based on the ESP32 microcontroller that boasts Wifi, Bluetooth, Ethernet and Low Power support all in a single chip. (vanepp) made breadboard work, adjusted pin numbering and labels and reduced size of schematic and cleaned up pcb. This chip is 30pins long (2 x15) and 11 pins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
  Keypad Membran 4x4: Membrane Keypad 4x4 Matrix
