# Fritzing sketch ESP32_RFID-RC522_Keypad_LCD (saved by Fritzing 1.0.3b)

parts:
  M1 = DOIT Esp32 DevKit v1 (30 pins long, 11 pins width) [part_number=ESP32S-PIN30]
  Componente1 = RFID-RC522-v3
  Keypad4x3 = Keypad Membran 4x4
  LCM1602_IIC2 = LCM1602 IIC [part_number="LCM1602 IIC" chip_label="LCM1602 IIC" package="DIP (Dual Inline) [THT]"]
  U2 = LCD-16X2 [package=lcd-16x2_noholes]
  JACK1 = 2.1mm Barrel Jack with Terminal Block

nets:
  3V3: M1.3V3, Componente1.3.3V
  GND: M1.GND, Componente1.GND, LCM1602_IIC2.GND, JACK1.NEG
  N1: M1.D15, Componente1.RST
  N2: M1.D4, Componente1.SDA
  N3: M1.D18, Componente1.SCK
  N4: M1.D19, Componente1.MISO
  N5: M1.D21, LCM1602_IIC2.SDA
  N6: M1.D22, LCM1602_IIC2.SCL
  N7: M1.D23, Componente1.MOSI
  N8: M1.D32, Keypad4x3.Pin8
  N9: M1.D33, Keypad4x3.Pin7
  N10: M1.D25, Keypad4x3.Pin6
  N11: M1.D26, Keypad4x3.Pin5
  N12: M1.D27, Keypad4x3.Pin4
  N13: M1.D14, Keypad4x3.Pin3
  N14: M1.D12, Keypad4x3.Pin2
  N15: M1.D13, Keypad4x3.Pin1
  VIN: M1.VIN, LCM1602_IIC2.VCC, JACK1.POS
  VSS: LCM1602_IIC2.VSS, U2.VSS
  VDD: LCM1602_IIC2.VDD, U2.VDD
  N16: LCM1602_IIC2.V0, U2.VO
  N17: LCM1602_IIC2.RS, U2.RS
  N18: LCM1602_IIC2.RW, U2.R_W
  N19: LCM1602_IIC2.E, U2.E
  N20: LCM1602_IIC2.D0, U2.DB0
  N21: LCM1602_IIC2.D1, U2.DB1
  N22: LCM1602_IIC2.D2, U2.DB2
  N23: LCM1602_IIC2.D3, U2.DB3
  N24: LCM1602_IIC2.D4, U2.DB4
  N25: LCM1602_IIC2.D5, U2.DB5
  N26: LCM1602_IIC2.D6, U2.DB6
  N27: LCM1602_IIC2.D7, U2.DB7
  N28: LCM1602_IIC2.A, U2.A
  N29: LCM1602_IIC2.K, U2.K
  N30: LCM1602_IIC2.LED_A, LCM1602_IIC2.LED_B

notes:
  5 Volts

custom parts:
  DOIT Esp32 DevKit v1 (30 pins long, 11 pins width): The DOIT Esp32 DevKit v1 is one of the development board created by DOIT to evaluate the ESP-WROOM-32 module. It is based on the ESP32 microcontroller that boasts Wifi, Bluetooth, Ethernet and Low Power support all in a single chip. (vanepp) made breadboard work, adjusted pin numbering and labels and reduced size of schematic and cleaned up pcb. This chip is 30pins long (2 x15) and 11 pins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
  RFID-RC522-v3: A simple China made RFID-RC522 Reader (6x4 cm); do check the pin labels, as this is a MFRC522 based clone.
  Keypad Membran 4x4: Membrane Keypad 4x4 Matrix
  LCM1602 IIC: I2C-Module to use a 1602 or 2004 LCD on with the wire.h libory Serial LCD Modul
